// Logisim project And_de_4bits.circ as structural Verilog: 4 circuits, main circuit main
module main (
  output [31:0] out_1
);

  wire undriven, undriven_2, undriven_3, undriven_4, undriven_5, undriven_6, undriven_7, undriven_8,
       undriven_9, undriven_10, undriven_11, undriven_12, undriven_13, undriven_14, undriven_15, undriven_16,
       undriven_17, undriven_18, undriven_19, undriven_20, undriven_21, undriven_22, undriven_23,
       undriven_24, undriven_25, undriven_26, undriven_27, undriven_28, undriven_29, undriven_30,
       undriven_31, undriven_32, undriven_33, undriven_34, undriven_35, undriven_36, undriven_37,
       undriven_38, undriven_39, undriven_40, undriven_41, undriven_42, undriven_43, undriven_44,
       undriven_45, undriven_46, undriven_47, undriven_48, undriven_49, undriven_50, undriven_51,
       undriven_52, undriven_53, undriven_54, undriven_55, undriven_56;

  AND_32_BITS and_32_bits_1 (
    .A(undriven_2), .in_2(undriven_3), .A_8(undriven_4), .A_12(undriven_5), .in_5(undriven_6),
    .in_6(undriven_7), .in_7(undriven_8), .in_8(undriven_9), .A_1(undriven_10), .in_10(undriven_11),
    .A_9(undriven_12), .A_13(undriven_13), .in_13(undriven_14), .in_14(undriven_15), .in_15(undriven_16),
    .in_16(undriven_17), .A_2(undriven_18), .in_18(undriven_19), .A_10(undriven_20), .A_14(undriven_21),
    .in_21(undriven_22), .in_22(undriven_23), .in_23(undriven_24), .in_24(undriven_25), .A_3(undriven_26),
    .in_26(undriven_27), .A_11(undriven_28), .A_15(undriven_29), .in_29(undriven_30), .in_30(undriven_31),
    .in_31(undriven_32), .in_32(undriven_33), .A_16(undriven_34), .A_20(undriven_35), .A_24(undriven_36),
    .A_28(undriven_37), .in_37(undriven_38), .in_38(undriven_39), .in_39(undriven_40), .in_40(undriven_41),
    .A_17(undriven_42), .A_21(undriven_43), .A_25(undriven_44), .A_29(undriven), .in_45(undriven_45),
    .in_46(undriven_46), .in_47(undriven_47), .in_48(undriven_48), .A_18(undriven_49), .A_22(undriven_50),
    .A_26(undriven_51), .A_30(undriven_52), .in_53(undriven_53), .in_54(undriven_54), .in_55(undriven_55),
    .in_56(undriven_56), .out_65(out_1));  // open: A_19, A_23, A_27, A_31, in_61, in_62, in_63, in_64
endmodule

module And4bits (
  input  A,
  input  B,
  input  A_1,
  input  B_1,
  input  A_2,
  input  B_2,
  input  A_3,
  input  B_3,
  output S,
  output S_1,
  output S_2,
  output S_3
);

  and and_1 (S, A, B);
  and and_2 (S_1, A_1, B_1);
  and and_3 (S_2, A_2, B_2);
  and and_4 (S_3, A_3, B_3);
endmodule

module AND_1_BIT (
  input  A,
  input  B,
  output S
);

  and and_1 (S, A, B);
endmodule

module AND_32_BITS (
  input  A,
  input  in_2,
  input  A_8,
  input  A_12,
  input  in_5,
  input  in_6,
  input  in_7,
  input  in_8,
  input  A_1,
  input  in_10,
  input  A_9,
  input  A_13,
  input  in_13,
  input  in_14,
  input  in_15,
  input  in_16,
  input  A_2,
  input  in_18,
  input  A_10,
  input  A_14,
  input  in_21,
  input  in_22,
  input  in_23,
  input  in_24,
  input  A_3,
  input  in_26,
  input  A_11,
  input  A_15,
  input  in_29,
  input  in_30,
  input  in_31,
  input  in_32,
  input  A_16,
  input  A_20,
  input  A_24,
  input  A_28,
  input  in_37,
  input  in_38,
  input  in_39,
  input  in_40,
  input  A_17,
  input  A_21,
  input  A_25,
  input  A_29,
  input  in_45,
  input  in_46,
  input  in_47,
  input  in_48,
  input  A_18,
  input  A_22,
  input  A_26,
  input  A_30,
  input  in_53,
  input  in_54,
  input  in_55,
  input  in_56,
  input  A_19,
  input  A_23,
  input  A_27,
  input  A_31,
  input  in_61,
  input  in_62,
  input  in_63,
  input  in_64,
  output [31:0] out_65
);

  And4bits and4bits_1 (
    .B(in_5), .A_1(A_1), .B_1(in_13), .A_2(A_2), .B_2(in_21), .A_3(A_3), .B_3(in_29), .A(A), .S(out_65[0]),
    .S_1(out_65[1]), .S_2(out_65[2]), .S_3(out_65[3]));
  And4bits and4bits_2 (
    .B(in_37), .A_1(A_17), .B_1(in_45), .A_2(A_18), .B_2(in_53), .A_3(A_19), .B_3(in_61), .A(A_16),
    .S(out_65[16]), .S_1(out_65[17]), .S_2(out_65[18]), .S_3(out_65[19]));
  And4bits and4bits_3 (
    .B(in_6), .A_1(in_10), .B_1(in_14), .A_2(in_18), .B_2(in_22), .A_3(in_26), .B_3(in_30), .A(in_2),
    .S(out_65[4]), .S_1(out_65[5]), .S_2(out_65[6]), .S_3(out_65[7]));
  And4bits and4bits_4 (
    .B(in_38), .A_1(A_21), .B_1(in_46), .A_2(A_22), .B_2(in_54), .A_3(A_23), .B_3(in_62), .A(A_20),
    .S(out_65[20]), .S_1(out_65[21]), .S_2(out_65[22]), .S_3(out_65[23]));
  And4bits and4bits_5 (
    .B(in_7), .A_1(A_9), .B_1(in_15), .A_2(A_10), .B_2(in_23), .A_3(A_11), .B_3(in_31), .A(A_8),
    .S(out_65[8]), .S_1(out_65[9]), .S_2(out_65[10]), .S_3(out_65[11]));
  And4bits and4bits_6 (
    .B(in_39), .A_1(A_25), .B_1(in_47), .A_2(A_26), .B_2(in_55), .A_3(A_27), .B_3(in_63), .A(A_24),
    .S(out_65[24]), .S_1(out_65[25]), .S_2(out_65[26]), .S_3(out_65[27]));
  And4bits and4bits_7 (
    .B(in_8), .A_1(A_13), .B_1(in_16), .A_2(A_14), .B_2(in_24), .A_3(A_15), .B_3(in_32), .A(A_12),
    .S(out_65[12]), .S_1(out_65[13]), .S_2(out_65[14]), .S_3(out_65[15]));
  And4bits and4bits_8 (
    .B(in_40), .A_1(A_29), .B_1(in_48), .A_2(A_30), .B_2(in_56), .A_3(A_31), .B_3(in_64), .A(A_28),
    .S(out_65[28]), .S_1(out_65[29]), .S_2(out_65[30]), .S_3(out_65[31]));
endmodule
