// Logisim project Trabalho_logica_digital.circ as structural Verilog
module adicao_1bit (
  input  A,
  input  B,
  input  Carry_in,
  output SUM,
  output Carry_out
);

  wire and_1_out, and_2_out, xor_1_out;

  xor xor_1 (xor_1_out, B, A);
  and and_1 (and_1_out, B, A);
  xor xor_2 (SUM, xor_1_out, Carry_in);
  and and_2 (and_2_out, xor_1_out, Carry_in);
  or or_1 (Carry_out, and_2_out, and_1_out);
endmodule

module adicao_32bit (
  input  A_0,
  input  A_1,
  input  A_2,
  input  A_3,
  input  B_0,
  input  B_1,
  input  B_2,
  input  B_3,
  input  A_4,
  input  A_5,
  input  A_6,
  input  A_7,
  input  B_4,
  input  B_5,
  input  B_6,
  input  B_7,
  input  A_8,
  input  A_9,
  input  A_10,
  input  A_11,
  input  B_8,
  input  B_9,
  input  B_10,
  input  B_11,
  input  A_12,
  input  A_13,
  input  A_14,
  input  A_15,
  input  B_12,
  input  B_13,
  input  B_14,
  input  B_15,
  input  A_16,
  input  A_17,
  input  A_18,
  input  A_19,
  input  B_16,
  input  B_17,
  input  B_18,
  input  B_19,
  input  A_20,
  input  A_21,
  input  A_22,
  input  A_23,
  input  B_20,
  input  B_21,
  input  B_22,
  input  B_23,
  input  A_24,
  input  A_25,
  input  A_26,
  input  A_27,
  input  B_24,
  input  B_25,
  input  B_26,
  input  B_27,
  input  A_28,
  input  A_29,
  input  A_30,
  input  A_31,
  input  B_28,
  input  B_29,
  input  B_30,
  input  B_31,
  output S_0,
  output S_1,
  output S_2,
  output S_3,
  output S_4,
  output S_5,
  output S_6,
  output S_7,
  output S_8,
  output S_9,
  output S_10,
  output S_11,
  output S_12,
  output S_13,
  output S_14,
  output S_15,
  output S_16,
  output S_17,
  output S_18,
  output S_19,
  output S_20,
  output S_21,
  output S_22,
  output S_23,
  output S_24,
  output S_25,
  output S_26,
  output S_27,
  output S_28,
  output S_29,
  output S_30,
  output S_31,
  output OVERFLOW
);

  wire adicao_1bit_1_carry_out, adicao_1bit_2_carry_out, adicao_1bit_3_carry_out, adicao_1bit_4_carry_out,
       adicao_1bit_5_carry_out, adicao_1bit_6_carry_out, adicao_1bit_7_carry_out, adicao_1bit_8_carry_out,
       adicao_1bit_9_carry_out, adicao_1bit_10_carry_out, adicao_1bit_11_carry_out, adicao_1bit_12_carry_out,
       adicao_1bit_13_carry_out, adicao_1bit_14_carry_out, adicao_1bit_15_carry_out,
       adicao_1bit_16_carry_out, adicao_1bit_17_carry_out, adicao_1bit_18_carry_out,
       adicao_1bit_19_carry_out, adicao_1bit_20_carry_out, adicao_1bit_21_carry_out,
       adicao_1bit_22_carry_out, adicao_1bit_23_carry_out, adicao_1bit_24_carry_out,
       adicao_1bit_25_carry_out, adicao_1bit_26_carry_out, adicao_1bit_27_carry_out,
       adicao_1bit_28_carry_out, adicao_1bit_29_carry_out, adicao_1bit_30_carry_out, adicao_1bit_31_carry_out;

  adicao_1bit adicao_1bit_1 (.A(A_0), .B(B_0), .Carry_in(1'b0), .SUM(S_0), .Carry_out(adicao_1bit_1_carry_out));
  adicao_1bit adicao_1bit_2 (
    .A(A_4), .B(B_4), .Carry_in(adicao_1bit_25_carry_out), .SUM(S_4), .Carry_out(adicao_1bit_2_carry_out));
  adicao_1bit adicao_1bit_3 (
    .A(A_8), .B(B_8), .Carry_in(adicao_1bit_26_carry_out), .SUM(S_8), .Carry_out(adicao_1bit_3_carry_out));
  adicao_1bit adicao_1bit_4 (
    .A(A_12), .B(B_12), .Carry_in(adicao_1bit_27_carry_out), .SUM(S_12), .Carry_out(adicao_1bit_4_carry_out));
  adicao_1bit adicao_1bit_5 (
    .A(A_16), .B(B_16), .Carry_in(adicao_1bit_28_carry_out), .SUM(S_16), .Carry_out(adicao_1bit_5_carry_out));
  adicao_1bit adicao_1bit_6 (
    .A(A_20), .B(B_20), .Carry_in(adicao_1bit_29_carry_out), .SUM(S_20), .Carry_out(adicao_1bit_6_carry_out));
  adicao_1bit adicao_1bit_7 (
    .A(A_24), .B(B_24), .Carry_in(adicao_1bit_30_carry_out), .SUM(S_24), .Carry_out(adicao_1bit_7_carry_out));
  adicao_1bit adicao_1bit_8 (
    .A(A_28), .B(B_28), .Carry_in(adicao_1bit_31_carry_out), .SUM(S_28), .Carry_out(adicao_1bit_8_carry_out));
  adicao_1bit adicao_1bit_9 (
    .A(A_1), .B(B_1), .Carry_in(adicao_1bit_1_carry_out), .SUM(S_1), .Carry_out(adicao_1bit_9_carry_out));
  adicao_1bit adicao_1bit_10 (
    .A(A_5), .B(B_5), .Carry_in(adicao_1bit_2_carry_out), .SUM(S_5), .Carry_out(adicao_1bit_10_carry_out));
  adicao_1bit adicao_1bit_11 (
    .A(A_9), .B(B_9), .Carry_in(adicao_1bit_3_carry_out), .SUM(S_9), .Carry_out(adicao_1bit_11_carry_out));
  adicao_1bit adicao_1bit_12 (
    .A(A_13), .B(B_13), .Carry_in(adicao_1bit_4_carry_out), .SUM(S_13), .Carry_out(adicao_1bit_12_carry_out));
  adicao_1bit adicao_1bit_13 (
    .A(A_17), .B(B_17), .Carry_in(adicao_1bit_5_carry_out), .SUM(S_17), .Carry_out(adicao_1bit_13_carry_out));
  adicao_1bit adicao_1bit_14 (
    .A(A_21), .B(B_21), .Carry_in(adicao_1bit_6_carry_out), .SUM(S_21), .Carry_out(adicao_1bit_14_carry_out));
  adicao_1bit adicao_1bit_15 (
    .A(A_25), .B(B_25), .Carry_in(adicao_1bit_7_carry_out), .SUM(S_25), .Carry_out(adicao_1bit_15_carry_out));
  adicao_1bit adicao_1bit_16 (
    .A(A_29), .B(B_29), .Carry_in(adicao_1bit_8_carry_out), .SUM(S_29), .Carry_out(adicao_1bit_16_carry_out));
  adicao_1bit adicao_1bit_17 (
    .A(A_2), .B(B_2), .Carry_in(adicao_1bit_9_carry_out), .SUM(S_2), .Carry_out(adicao_1bit_17_carry_out));
  adicao_1bit adicao_1bit_18 (
    .A(A_6), .B(B_6), .Carry_in(adicao_1bit_10_carry_out), .SUM(S_6), .Carry_out(adicao_1bit_18_carry_out));
  adicao_1bit adicao_1bit_19 (
    .A(A_10), .B(B_10), .Carry_in(adicao_1bit_11_carry_out), .SUM(S_10), .Carry_out(adicao_1bit_19_carry_out));
  adicao_1bit adicao_1bit_20 (
    .A(A_14), .B(B_14), .Carry_in(adicao_1bit_12_carry_out), .SUM(S_14), .Carry_out(adicao_1bit_20_carry_out));
  adicao_1bit adicao_1bit_21 (
    .A(A_18), .B(B_18), .Carry_in(adicao_1bit_13_carry_out), .SUM(S_18), .Carry_out(adicao_1bit_21_carry_out));
  adicao_1bit adicao_1bit_22 (
    .A(A_22), .B(B_22), .Carry_in(adicao_1bit_14_carry_out), .SUM(S_22), .Carry_out(adicao_1bit_22_carry_out));
  adicao_1bit adicao_1bit_23 (
    .A(A_26), .B(B_26), .Carry_in(adicao_1bit_15_carry_out), .SUM(S_26), .Carry_out(adicao_1bit_23_carry_out));
  adicao_1bit adicao_1bit_24 (
    .A(A_30), .B(B_30), .Carry_in(adicao_1bit_16_carry_out), .SUM(S_30), .Carry_out(adicao_1bit_24_carry_out));
  adicao_1bit adicao_1bit_25 (
    .A(A_3), .B(B_3), .Carry_in(adicao_1bit_17_carry_out), .SUM(S_3), .Carry_out(adicao_1bit_25_carry_out));
  adicao_1bit adicao_1bit_26 (
    .A(A_7), .B(B_7), .Carry_in(adicao_1bit_18_carry_out), .SUM(S_7), .Carry_out(adicao_1bit_26_carry_out));
  adicao_1bit adicao_1bit_27 (
    .A(A_11), .B(B_11), .Carry_in(adicao_1bit_19_carry_out), .SUM(S_11), .Carry_out(adicao_1bit_27_carry_out));
  adicao_1bit adicao_1bit_28 (
    .A(A_15), .B(B_15), .Carry_in(adicao_1bit_20_carry_out), .SUM(S_15), .Carry_out(adicao_1bit_28_carry_out));
  adicao_1bit adicao_1bit_29 (
    .A(A_19), .B(B_19), .Carry_in(adicao_1bit_21_carry_out), .SUM(S_19), .Carry_out(adicao_1bit_29_carry_out));
  adicao_1bit adicao_1bit_30 (
    .A(A_23), .B(B_23), .Carry_in(adicao_1bit_22_carry_out), .SUM(S_23), .Carry_out(adicao_1bit_30_carry_out));
  adicao_1bit adicao_1bit_31 (
    .A(A_27), .B(B_27), .Carry_in(adicao_1bit_23_carry_out), .SUM(S_27), .Carry_out(adicao_1bit_31_carry_out));
  adicao_1bit adicao_1bit_32 (
    .A(A_31), .B(B_31), .Carry_in(adicao_1bit_24_carry_out), .SUM(S_31), .Carry_out(OVERFLOW));
endmodule

module subtracao_1bit (
  input  A,
  input  B,
  input  Carry_in,
  output SUB,
  output Carry_out
);

  wire not_1_out;

  not not_1 (not_1_out, B);
  adicao_1bit adicao_1bit_1 (.A(A), .B(not_1_out), .Carry_in(Carry_in), .SUM(SUB), .Carry_out(Carry_out));
endmodule

module subtracao_32bit (
  input  A_0,
  input  A_1,
  input  A_2,
  input  A_3,
  input  B_0,
  input  B_1,
  input  B_2,
  input  B_3,
  input  A_4,
  input  A_5,
  input  A_6,
  input  A_7,
  input  B_4,
  input  B_5,
  input  B_6,
  input  B_7,
  input  A_8,
  input  A_9,
  input  A_10,
  input  A_11,
  input  B_8,
  input  B_9,
  input  B_10,
  input  B_11,
  input  A_12,
  input  A_13,
  input  A_14,
  input  A_15,
  input  B_12,
  input  B_13,
  input  B_14,
  input  B_15,
  input  A_16,
  input  A_17,
  input  A_18,
  input  A_19,
  input  B_16,
  input  B_17,
  input  B_18,
  input  B_19,
  input  A_20,
  input  A_21,
  input  A_22,
  input  A_23,
  input  B_20,
  input  B_21,
  input  B_22,
  input  B_23,
  input  A_24,
  input  A_25,
  input  A_26,
  input  A_27,
  input  B_24,
  input  B_25,
  input  B_26,
  input  B_27,
  input  A_28,
  input  A_29,
  input  A_30,
  input  A_31,
  input  B_28,
  input  B_29,
  input  B_30,
  input  B_31,
  output S_0,
  output S_1,
  output S_2,
  output S_3,
  output S_4,
  output S_5,
  output S_6,
  output S_7,
  output S_8,
  output S_9,
  output S_10,
  output S_11,
  output S_12,
  output S_13,
  output S_14,
  output S_15,
  output S_16,
  output S_17,
  output S_18,
  output S_19,
  output S_20,
  output S_21,
  output S_22,
  output S_23,
  output S_24,
  output S_25,
  output S_26,
  output S_27,
  output S_28,
  output S_29,
  output S_30,
  output S_31,
  output Negativo
);

  wire subtracao_1bit_1_carry_out, subtracao_1bit_2_carry_out, subtracao_1bit_3_carry_out,
       subtracao_1bit_4_carry_out, subtracao_1bit_5_carry_out, subtracao_1bit_6_carry_out,
       subtracao_1bit_7_carry_out, subtracao_1bit_8_carry_out, subtracao_1bit_9_carry_out,
       subtracao_1bit_10_carry_out, subtracao_1bit_11_carry_out, subtracao_1bit_12_carry_out,
       subtracao_1bit_13_carry_out, subtracao_1bit_14_carry_out, subtracao_1bit_15_carry_out,
       subtracao_1bit_16_carry_out, subtracao_1bit_17_carry_out, subtracao_1bit_18_carry_out,
       subtracao_1bit_19_carry_out, subtracao_1bit_20_carry_out, subtracao_1bit_21_carry_out,
       subtracao_1bit_22_carry_out, subtracao_1bit_23_carry_out, subtracao_1bit_24_carry_out,
       subtracao_1bit_25_carry_out, subtracao_1bit_26_carry_out, subtracao_1bit_27_carry_out,
       subtracao_1bit_28_carry_out, subtracao_1bit_29_carry_out, subtracao_1bit_30_carry_out,
       subtracao_1bit_31_carry_out, subtracao_1bit_32_carry_out;

  subtracao_1bit subtracao_1bit_1 (
    .A(A_0), .B(B_0), .Carry_in(1'b1), .SUB(S_0), .Carry_out(subtracao_1bit_1_carry_out));
  subtracao_1bit subtracao_1bit_2 (
    .A(A_4), .B(B_4), .Carry_in(subtracao_1bit_25_carry_out), .SUB(S_4),
    .Carry_out(subtracao_1bit_2_carry_out));
  subtracao_1bit subtracao_1bit_3 (
    .A(A_8), .B(B_8), .Carry_in(subtracao_1bit_26_carry_out), .SUB(S_8),
    .Carry_out(subtracao_1bit_3_carry_out));
  subtracao_1bit subtracao_1bit_4 (
    .A(A_12), .B(B_12), .Carry_in(subtracao_1bit_27_carry_out), .SUB(S_12),
    .Carry_out(subtracao_1bit_4_carry_out));
  subtracao_1bit subtracao_1bit_5 (
    .A(A_16), .B(B_16), .Carry_in(subtracao_1bit_28_carry_out), .SUB(S_16),
    .Carry_out(subtracao_1bit_5_carry_out));
  subtracao_1bit subtracao_1bit_6 (
    .A(A_20), .B(B_20), .Carry_in(subtracao_1bit_29_carry_out), .SUB(S_20),
    .Carry_out(subtracao_1bit_6_carry_out));
  subtracao_1bit subtracao_1bit_7 (
    .A(A_24), .B(B_24), .Carry_in(subtracao_1bit_30_carry_out), .SUB(S_24),
    .Carry_out(subtracao_1bit_7_carry_out));
  subtracao_1bit subtracao_1bit_8 (
    .A(A_28), .B(B_28), .Carry_in(subtracao_1bit_31_carry_out), .SUB(S_28),
    .Carry_out(subtracao_1bit_8_carry_out));
  subtracao_1bit subtracao_1bit_9 (
    .A(A_1), .B(B_1), .Carry_in(subtracao_1bit_1_carry_out), .SUB(S_1), .Carry_out(subtracao_1bit_9_carry_out));
  subtracao_1bit subtracao_1bit_10 (
    .A(A_5), .B(B_5), .Carry_in(subtracao_1bit_2_carry_out), .SUB(S_5),
    .Carry_out(subtracao_1bit_10_carry_out));
  subtracao_1bit subtracao_1bit_11 (
    .A(A_9), .B(B_9), .Carry_in(subtracao_1bit_3_carry_out), .SUB(S_9),
    .Carry_out(subtracao_1bit_11_carry_out));
  subtracao_1bit subtracao_1bit_12 (
    .A(A_13), .B(B_13), .Carry_in(subtracao_1bit_4_carry_out), .SUB(S_13),
    .Carry_out(subtracao_1bit_12_carry_out));
  subtracao_1bit subtracao_1bit_13 (
    .A(A_17), .B(B_17), .Carry_in(subtracao_1bit_5_carry_out), .SUB(S_17),
    .Carry_out(subtracao_1bit_13_carry_out));
  subtracao_1bit subtracao_1bit_14 (
    .A(A_21), .B(B_21), .Carry_in(subtracao_1bit_6_carry_out), .SUB(S_21),
    .Carry_out(subtracao_1bit_14_carry_out));
  subtracao_1bit subtracao_1bit_15 (
    .A(A_25), .B(B_25), .Carry_in(subtracao_1bit_7_carry_out), .SUB(S_25),
    .Carry_out(subtracao_1bit_15_carry_out));
  subtracao_1bit subtracao_1bit_16 (
    .A(A_29), .B(B_29), .Carry_in(subtracao_1bit_8_carry_out), .SUB(S_29),
    .Carry_out(subtracao_1bit_16_carry_out));
  subtracao_1bit subtracao_1bit_17 (
    .A(A_2), .B(B_2), .Carry_in(subtracao_1bit_9_carry_out), .SUB(S_2),
    .Carry_out(subtracao_1bit_17_carry_out));
  subtracao_1bit subtracao_1bit_18 (
    .A(A_6), .B(B_6), .Carry_in(subtracao_1bit_10_carry_out), .SUB(S_6),
    .Carry_out(subtracao_1bit_18_carry_out));
  subtracao_1bit subtracao_1bit_19 (
    .A(A_10), .B(B_10), .Carry_in(subtracao_1bit_11_carry_out), .SUB(S_10),
    .Carry_out(subtracao_1bit_19_carry_out));
  subtracao_1bit subtracao_1bit_20 (
    .A(A_14), .B(B_14), .Carry_in(subtracao_1bit_12_carry_out), .SUB(S_14),
    .Carry_out(subtracao_1bit_20_carry_out));
  subtracao_1bit subtracao_1bit_21 (
    .A(A_18), .B(B_18), .Carry_in(subtracao_1bit_13_carry_out), .SUB(S_18),
    .Carry_out(subtracao_1bit_21_carry_out));
  subtracao_1bit subtracao_1bit_22 (
    .A(A_22), .B(B_22), .Carry_in(subtracao_1bit_14_carry_out), .SUB(S_22),
    .Carry_out(subtracao_1bit_22_carry_out));
  subtracao_1bit subtracao_1bit_23 (
    .A(A_26), .B(B_26), .Carry_in(subtracao_1bit_15_carry_out), .SUB(S_26),
    .Carry_out(subtracao_1bit_23_carry_out));
  subtracao_1bit subtracao_1bit_24 (
    .A(A_30), .B(B_30), .Carry_in(subtracao_1bit_16_carry_out), .SUB(S_30),
    .Carry_out(subtracao_1bit_24_carry_out));
  subtracao_1bit subtracao_1bit_25 (
    .A(A_3), .B(B_3), .Carry_in(subtracao_1bit_17_carry_out), .SUB(S_3),
    .Carry_out(subtracao_1bit_25_carry_out));
  subtracao_1bit subtracao_1bit_26 (
    .A(A_7), .B(B_7), .Carry_in(subtracao_1bit_18_carry_out), .SUB(S_7),
    .Carry_out(subtracao_1bit_26_carry_out));
  subtracao_1bit subtracao_1bit_27 (
    .A(A_11), .B(B_11), .Carry_in(subtracao_1bit_19_carry_out), .SUB(S_11),
    .Carry_out(subtracao_1bit_27_carry_out));
  subtracao_1bit subtracao_1bit_28 (
    .A(A_15), .B(B_15), .Carry_in(subtracao_1bit_20_carry_out), .SUB(S_15),
    .Carry_out(subtracao_1bit_28_carry_out));
  subtracao_1bit subtracao_1bit_29 (
    .A(A_19), .B(B_19), .Carry_in(subtracao_1bit_21_carry_out), .SUB(S_19),
    .Carry_out(subtracao_1bit_29_carry_out));
  subtracao_1bit subtracao_1bit_30 (
    .A(A_23), .B(B_23), .Carry_in(subtracao_1bit_22_carry_out), .SUB(S_23),
    .Carry_out(subtracao_1bit_30_carry_out));
  subtracao_1bit subtracao_1bit_31 (
    .A(A_27), .B(B_27), .Carry_in(subtracao_1bit_23_carry_out), .SUB(S_27),
    .Carry_out(subtracao_1bit_31_carry_out));
  subtracao_1bit subtracao_1bit_32 (
    .A(A_31), .B(B_31), .Carry_in(subtracao_1bit_24_carry_out), .SUB(S_31),
    .Carry_out(subtracao_1bit_32_carry_out));
  not not_1 (Negativo, subtracao_1bit_32_carry_out);
endmodule

module slt (
  input  A_0,
  input  A_1,
  input  A_2,
  input  A_3,
  input  A_4,
  input  A_5,
  input  A_6,
  input  A_7,
  input  A_8,
  input  A_9,
  input  A_10,
  input  A_11,
  input  A_12,
  input  A_13,
  input  A_14,
  input  A_15,
  input  A_16,
  input  A_17,
  input  A_18,
  input  A_19,
  input  A_20,
  input  A_21,
  input  A_22,
  input  A_23,
  input  A_24,
  input  A_25,
  input  A_26,
  input  A_27,
  input  A_28,
  input  A_29,
  input  A_30,
  input  A_31,
  input  B_0,
  input  B_1,
  input  B_2,
  input  B_3,
  input  B_4,
  input  B_5,
  input  B_6,
  input  B_7,
  input  B_8,
  input  B_9,
  input  B_10,
  input  B_11,
  input  B_12,
  input  B_13,
  input  B_14,
  input  B_15,
  input  B_16,
  input  B_17,
  input  B_18,
  input  B_19,
  input  B_20,
  input  B_21,
  input  B_22,
  input  B_23,
  input  B_24,
  input  B_25,
  input  B_26,
  input  B_27,
  input  B_28,
  input  B_29,
  input  B_30,
  input  B_31,
  output Resultado_0,
  output Resultado_1,
  output Resultado_2,
  output Resultado_3,
  output Resultado_4,
  output Resultado_5,
  output Resultado_6,
  output Resultado_7,
  output Resultado_8,
  output Resultado_9,
  output Resultado_10,
  output Resultado_11,
  output Resultado_12,
  output Resultado_13,
  output Resultado_14,
  output Resultado_15
);

  wire subtracao_32bit_1_negativo;

  subtracao_32bit subtracao_32bit_1 (
    .A_7(A_7), .B_7(B_7), .A_11(A_11), .B_11(B_11), .A_3(A_3), .A_15(A_15), .B_15(B_15), .A_19(A_19),
    .B_19(B_19), .B_3(B_3), .A_23(A_23), .B_23(B_23), .A_27(A_27), .B_27(B_27), .A_31(A_31), .B_31(B_31),
    .A_5(A_5), .B_5(B_5), .A_9(A_9), .B_9(B_9), .A_1(A_1), .A_13(A_13), .B_13(B_13), .A_17(A_17),
    .B_17(B_17), .B_1(B_1), .A_21(A_21), .B_21(B_21), .A_25(A_25), .B_25(B_25), .A_29(A_29), .B_29(B_29),
    .A_6(A_6), .B_6(B_6), .A_10(A_10), .B_10(B_10), .A_2(A_2), .A_14(A_14), .B_14(B_14), .A_18(A_18),
    .B_18(B_18), .B_2(B_2), .A_22(A_22), .B_22(B_22), .A_26(A_26), .B_26(B_26), .A_30(A_30), .B_30(B_30),
    .A_4(A_4), .B_4(B_4), .A_8(A_8), .B_8(B_8), .A_0(A_0), .A_12(A_12), .B_12(B_12), .A_16(A_16),
    .B_16(B_16), .B_0(B_0), .A_20(A_20), .B_20(B_20), .A_24(A_24), .B_24(B_24), .A_28(A_28), .B_28(B_28),
    .Negativo(subtracao_32bit_1_negativo));  // open: S_6, S_10, S_2, S_14, S_18, S_22, S_26, S_30, S_7, S_11, S_3, S_15, S_19, S_23, S_27, S_31, S_4, S_8, S_0, S_12, S_16, S_20, S_24, S_28, S_5, S_9, S_1, S_13, S_17, S_21, S_25, S_29
  assign {Resultado_15, Resultado_14, Resultado_13, Resultado_12, Resultado_11, Resultado_10, Resultado_9, Resultado_8, Resultado_7, Resultado_6, Resultado_5, Resultado_4, Resultado_3, Resultado_2, Resultado_1, Resultado_0} = {{15{1'b0}}, subtracao_32bit_1_negativo};  // Bit_Extender bit_extender_1
endmodule

module mux_2_para_1 (
  input  AluOp,
  input  A,
  input  B,
  output out_4,
  output out_5
);

  and and_1 (out_4, AluOp, A);
  and and_2 (out_5, ~AluOp, B);  // AND_Gate
endmodule

module bloco_artmetico (
  input  [31:0] in_1,
  input  [31:0] in_2
);

  adicao_32bit adicao_32bit_1 (
    .A_4(in_1[4]), .B_4(in_2[4]), .A_8(in_1[8]), .B_8(in_2[8]), .A_12(in_1[12]), .B_12(in_2[12]),
    .A_16(in_1[16]), .B_16(in_2[16]), .A_20(in_1[20]), .B_20(in_2[20]), .A_0(in_1[0]), .A_24(in_1[24]),
    .B_24(in_2[24]), .A_28(in_1[28]), .B_28(in_2[28]), .B_0(in_2[0]), .A_7(in_1[7]), .B_7(in_2[7]),
    .A_11(in_1[11]), .B_11(in_2[11]), .A_15(in_1[15]), .B_15(in_2[15]), .A_19(in_1[19]), .B_19(in_2[19]),
    .A_23(in_1[23]), .B_23(in_2[23]), .A_3(in_1[3]), .A_27(in_1[27]), .B_27(in_2[27]), .A_31(in_1[31]),
    .B_31(in_2[31]), .B_3(in_2[3]), .A_5(in_1[5]), .B_5(in_2[5]), .A_9(in_1[9]), .B_9(in_2[9]),
    .A_13(in_1[13]), .B_13(in_2[13]), .A_17(in_1[17]), .B_17(in_2[17]), .A_21(in_1[21]), .B_21(in_2[21]),
    .A_1(in_1[1]), .A_25(in_1[25]), .B_25(in_2[25]), .A_29(in_1[29]), .B_29(in_2[29]), .B_1(in_2[1]),
    .A_6(in_1[6]), .B_6(in_2[6]), .A_10(in_1[10]), .B_10(in_2[10]), .A_14(in_1[14]), .B_14(in_2[14]),
    .A_18(in_1[18]), .B_18(in_2[18]), .A_22(in_1[22]), .B_22(in_2[22]), .A_2(in_1[2]), .A_26(in_1[26]),
    .B_26(in_2[26]), .A_30(in_1[30]), .B_30(in_2[30]), .B_2(in_2[2]));  // open: S_6, S_10, S_14, S_18, S_22, S_2, S_26, S_30, S_7, S_11, S_15, S_19, S_23, S_3, S_27, S_31, OVERFLOW, S_4, S_8, S_12, S_16, S_20, S_0, S_24, S_28, S_5, S_9, S_13, S_17, S_21, S_1, S_25, S_29
  subtracao_32bit subtracao_32bit_1 (
    .A_7(in_1[7]), .B_7(in_2[7]), .A_11(in_1[11]), .B_11(in_2[11]), .A_3(in_1[3]), .A_15(in_1[15]),
    .B_15(in_2[15]), .A_19(in_1[19]), .B_19(in_2[19]), .B_3(in_2[3]), .A_23(in_1[23]), .B_23(in_2[23]),
    .A_27(in_1[27]), .B_27(in_2[27]), .A_31(in_1[31]), .B_31(in_2[31]), .A_5(in_1[5]), .B_5(in_2[5]),
    .A_9(in_1[9]), .B_9(in_2[9]), .A_1(in_1[1]), .A_13(in_1[13]), .B_13(in_2[13]), .A_17(in_1[17]),
    .B_17(in_2[17]), .B_1(in_2[1]), .A_21(in_1[21]), .B_21(in_2[21]), .A_25(in_1[25]), .B_25(in_2[25]),
    .A_29(in_1[29]), .B_29(in_2[29]), .A_6(in_1[6]), .B_6(in_2[6]), .A_10(in_1[10]), .B_10(in_2[10]),
    .A_2(in_1[2]), .A_14(in_1[14]), .B_14(in_2[14]), .A_18(in_1[18]), .B_18(in_2[18]), .B_2(in_2[2]),
    .A_22(in_1[22]), .B_22(in_2[22]), .A_26(in_1[26]), .B_26(in_2[26]), .A_30(in_1[30]), .B_30(in_2[30]),
    .A_4(in_1[4]), .B_4(in_2[4]), .A_8(in_1[8]), .B_8(in_2[8]), .A_0(in_1[0]), .A_12(in_1[12]),
    .B_12(in_2[12]), .A_16(in_1[16]), .B_16(in_2[16]), .B_0(in_2[0]), .A_20(in_1[20]), .B_20(in_2[20]),
    .A_24(in_1[24]), .B_24(in_2[24]), .A_28(in_1[28]), .B_28(in_2[28]));  // open: S_6, S_10, S_2, S_14, S_18, S_22, S_26, S_30, S_7, S_11, S_3, S_15, S_19, S_23, S_27, S_31, Negativo, S_4, S_8, S_0, S_12, S_16, S_20, S_24, S_28, S_5, S_9, S_1, S_13, S_17, S_21, S_25, S_29
  slt slt_1 ();  // open: A_0, A_1, A_2, A_3, A_4, A_5, A_6, A_7, A_8, A_9, A_10, A_11, A_12, A_13, A_14, A_15, A_16, A_17, A_18, A_19, A_20, A_21, A_22, A_23, A_24, A_25, A_26, A_27, A_28, A_29, A_30, A_31, B_0, B_1, B_2, B_3, B_4, B_5, B_6, B_7, B_8, B_9, B_10, B_11, B_12, B_13, B_14, B_15, B_16, B_17, B_18, B_19, B_20, B_21, B_22, B_23, B_24, B_25, B_26, B_27, B_28, B_29, B_30, B_31, Resultado_0, Resultado_1, Resultado_2, Resultado_3, Resultado_4, Resultado_5, Resultado_6, Resultado_7, Resultado_8, Resultado_9, Resultado_10, Resultado_11, Resultado_12, Resultado_13, Resultado_14, Resultado_15
endmodule
