// Logisim project Trabalho_logica_digital1.1.circ as structural Verilog: 15 circuits, main circuit main
module adicao_1bit (
  input  A,
  input  B,
  input  Carry_in,
  output SUM,
  output Carry_out
);

  wire and_1_out, and_2_out, xor_1_out;

  xor xor_1 (xor_1_out, B, A);
  and and_1 (and_1_out, B, A);
  xor xor_2 (SUM, xor_1_out, Carry_in);
  and and_2 (and_2_out, xor_1_out, Carry_in);
  or or_1 (Carry_out, and_2_out, and_1_out);
endmodule

module adicao_32bit (
  input  [31:0] A,
  input  [31:0] B,
  output [31:0] SUM,
  output Overflow
);

  wire adicao_1bit_1_carry_out, adicao_1bit_2_carry_out, adicao_1bit_3_carry_out, adicao_1bit_4_carry_out,
       adicao_1bit_5_carry_out, adicao_1bit_6_carry_out, adicao_1bit_7_carry_out, adicao_1bit_8_carry_out,
       adicao_1bit_9_carry_out, adicao_1bit_10_carry_out, adicao_1bit_11_carry_out, adicao_1bit_12_carry_out,
       adicao_1bit_13_carry_out, adicao_1bit_14_carry_out, adicao_1bit_15_carry_out,
       adicao_1bit_16_carry_out, adicao_1bit_17_carry_out, adicao_1bit_18_carry_out,
       adicao_1bit_19_carry_out, adicao_1bit_20_carry_out, adicao_1bit_21_carry_out,
       adicao_1bit_22_carry_out, adicao_1bit_23_carry_out, adicao_1bit_24_carry_out,
       adicao_1bit_25_carry_out, adicao_1bit_26_carry_out, adicao_1bit_27_carry_out,
       adicao_1bit_28_carry_out, adicao_1bit_29_carry_out, adicao_1bit_30_carry_out, adicao_1bit_31_carry_out;

  adicao_1bit adicao_1bit_1 (.Carry_in(1'b0), .A(A[0]), .B(B[0]), .SUM(SUM[0]), .Carry_out(adicao_1bit_1_carry_out));
  adicao_1bit adicao_1bit_2 (
    .Carry_in(adicao_1bit_1_carry_out), .A(A[1]), .B(B[1]), .SUM(SUM[1]), .Carry_out(adicao_1bit_2_carry_out));
  adicao_1bit adicao_1bit_3 (
    .Carry_in(adicao_1bit_2_carry_out), .A(A[2]), .B(B[2]), .SUM(SUM[2]), .Carry_out(adicao_1bit_3_carry_out));
  adicao_1bit adicao_1bit_4 (
    .Carry_in(adicao_1bit_3_carry_out), .A(A[3]), .B(B[3]), .SUM(SUM[3]), .Carry_out(adicao_1bit_4_carry_out));
  adicao_1bit adicao_1bit_5 (
    .Carry_in(adicao_1bit_4_carry_out), .A(A[4]), .B(B[4]), .SUM(SUM[4]), .Carry_out(adicao_1bit_5_carry_out));
  adicao_1bit adicao_1bit_6 (
    .Carry_in(adicao_1bit_5_carry_out), .A(A[5]), .B(B[5]), .SUM(SUM[5]), .Carry_out(adicao_1bit_6_carry_out));
  adicao_1bit adicao_1bit_7 (
    .Carry_in(adicao_1bit_6_carry_out), .A(A[6]), .B(B[6]), .SUM(SUM[6]), .Carry_out(adicao_1bit_7_carry_out));
  adicao_1bit adicao_1bit_8 (
    .Carry_in(adicao_1bit_7_carry_out), .A(A[7]), .B(B[7]), .SUM(SUM[7]), .Carry_out(adicao_1bit_8_carry_out));
  adicao_1bit adicao_1bit_9 (
    .Carry_in(adicao_1bit_8_carry_out), .A(A[8]), .B(B[8]), .SUM(SUM[8]), .Carry_out(adicao_1bit_9_carry_out));
  adicao_1bit adicao_1bit_10 (
    .Carry_in(adicao_1bit_9_carry_out), .A(A[9]), .B(B[9]), .SUM(SUM[9]), .Carry_out(adicao_1bit_10_carry_out));
  adicao_1bit adicao_1bit_11 (
    .Carry_in(adicao_1bit_10_carry_out), .A(A[10]), .B(B[10]), .SUM(SUM[10]),
    .Carry_out(adicao_1bit_11_carry_out));
  adicao_1bit adicao_1bit_12 (
    .Carry_in(adicao_1bit_11_carry_out), .A(A[11]), .B(B[11]), .SUM(SUM[11]),
    .Carry_out(adicao_1bit_12_carry_out));
  adicao_1bit adicao_1bit_13 (
    .Carry_in(adicao_1bit_12_carry_out), .A(A[12]), .B(B[12]), .SUM(SUM[12]),
    .Carry_out(adicao_1bit_13_carry_out));
  adicao_1bit adicao_1bit_14 (
    .Carry_in(adicao_1bit_13_carry_out), .A(A[13]), .B(B[13]), .SUM(SUM[13]),
    .Carry_out(adicao_1bit_14_carry_out));
  adicao_1bit adicao_1bit_15 (
    .Carry_in(adicao_1bit_14_carry_out), .A(A[14]), .B(B[14]), .SUM(SUM[14]),
    .Carry_out(adicao_1bit_15_carry_out));
  adicao_1bit adicao_1bit_16 (
    .Carry_in(adicao_1bit_15_carry_out), .A(A[15]), .B(B[15]), .SUM(SUM[15]),
    .Carry_out(adicao_1bit_16_carry_out));
  adicao_1bit adicao_1bit_17 (
    .Carry_in(adicao_1bit_16_carry_out), .A(A[16]), .B(B[16]), .SUM(SUM[16]),
    .Carry_out(adicao_1bit_17_carry_out));
  adicao_1bit adicao_1bit_18 (
    .Carry_in(adicao_1bit_17_carry_out), .A(A[17]), .B(B[17]), .SUM(SUM[17]),
    .Carry_out(adicao_1bit_18_carry_out));
  adicao_1bit adicao_1bit_19 (
    .Carry_in(adicao_1bit_18_carry_out), .A(A[18]), .B(B[18]), .SUM(SUM[18]),
    .Carry_out(adicao_1bit_19_carry_out));
  adicao_1bit adicao_1bit_20 (
    .Carry_in(adicao_1bit_19_carry_out), .A(A[19]), .B(B[19]), .SUM(SUM[19]),
    .Carry_out(adicao_1bit_20_carry_out));
  adicao_1bit adicao_1bit_21 (
    .Carry_in(adicao_1bit_20_carry_out), .A(A[20]), .B(B[20]), .SUM(SUM[20]),
    .Carry_out(adicao_1bit_21_carry_out));
  adicao_1bit adicao_1bit_22 (
    .Carry_in(adicao_1bit_21_carry_out), .A(A[21]), .B(B[21]), .SUM(SUM[21]),
    .Carry_out(adicao_1bit_22_carry_out));
  adicao_1bit adicao_1bit_23 (
    .Carry_in(adicao_1bit_22_carry_out), .A(A[22]), .B(B[22]), .SUM(SUM[22]),
    .Carry_out(adicao_1bit_23_carry_out));
  adicao_1bit adicao_1bit_24 (
    .Carry_in(adicao_1bit_23_carry_out), .A(A[23]), .B(B[23]), .SUM(SUM[23]),
    .Carry_out(adicao_1bit_24_carry_out));
  adicao_1bit adicao_1bit_25 (
    .Carry_in(adicao_1bit_24_carry_out), .A(A[24]), .B(B[24]), .SUM(SUM[24]),
    .Carry_out(adicao_1bit_25_carry_out));
  adicao_1bit adicao_1bit_26 (
    .Carry_in(adicao_1bit_25_carry_out), .A(A[25]), .B(B[25]), .SUM(SUM[25]),
    .Carry_out(adicao_1bit_26_carry_out));
  adicao_1bit adicao_1bit_27 (
    .Carry_in(adicao_1bit_26_carry_out), .A(A[26]), .B(B[26]), .SUM(SUM[26]),
    .Carry_out(adicao_1bit_27_carry_out));
  adicao_1bit adicao_1bit_28 (
    .Carry_in(adicao_1bit_27_carry_out), .A(A[27]), .B(B[27]), .SUM(SUM[27]),
    .Carry_out(adicao_1bit_28_carry_out));
  adicao_1bit adicao_1bit_29 (
    .Carry_in(adicao_1bit_28_carry_out), .A(A[28]), .B(B[28]), .SUM(SUM[28]),
    .Carry_out(adicao_1bit_29_carry_out));
  adicao_1bit adicao_1bit_30 (
    .Carry_in(adicao_1bit_29_carry_out), .A(A[29]), .B(B[29]), .SUM(SUM[29]),
    .Carry_out(adicao_1bit_30_carry_out));
  adicao_1bit adicao_1bit_31 (
    .Carry_in(adicao_1bit_30_carry_out), .A(A[30]), .B(B[30]), .SUM(SUM[30]),
    .Carry_out(adicao_1bit_31_carry_out));
  adicao_1bit adicao_1bit_32 (
    .Carry_in(adicao_1bit_31_carry_out), .A(A[31]), .B(B[31]), .SUM(SUM[31]), .Carry_out(Overflow));
endmodule

module subtracao_1bit (
  input  A,
  input  B,
  input  Carry_in,
  output SUB,
  output Carry_out
);

  wire not_1_out;

  not not_1 (not_1_out, B);
  adicao_1bit adicao_1bit_1 (.Carry_in(Carry_in), .A(A), .B(not_1_out), .SUM(SUB), .Carry_out(Carry_out));
endmodule

module subtracao_32bit (
  input  [31:0] A,
  input  [31:0] B,
  output [31:0] SUB,
  output Negativo,
  output Overflow
);

  wire subtracao_1bit_1_carry_out, subtracao_1bit_2_carry_out, subtracao_1bit_3_carry_out,
       subtracao_1bit_4_carry_out, subtracao_1bit_5_carry_out, subtracao_1bit_6_carry_out,
       subtracao_1bit_7_carry_out, subtracao_1bit_8_carry_out, subtracao_1bit_9_carry_out,
       subtracao_1bit_10_carry_out, subtracao_1bit_11_carry_out, subtracao_1bit_12_carry_out,
       subtracao_1bit_13_carry_out, subtracao_1bit_14_carry_out, subtracao_1bit_15_carry_out,
       subtracao_1bit_16_carry_out, subtracao_1bit_17_carry_out, subtracao_1bit_18_carry_out,
       subtracao_1bit_19_carry_out, subtracao_1bit_20_carry_out, subtracao_1bit_21_carry_out,
       subtracao_1bit_22_carry_out, subtracao_1bit_23_carry_out, subtracao_1bit_24_carry_out,
       subtracao_1bit_25_carry_out, subtracao_1bit_26_carry_out, subtracao_1bit_27_carry_out,
       subtracao_1bit_28_carry_out, subtracao_1bit_29_carry_out, subtracao_1bit_30_carry_out,
       subtracao_1bit_31_carry_out, subtracao_1bit_32_carry_out;

  subtracao_1bit subtracao_1bit_1 (
    .A(A[0]), .B(B[0]), .Carry_in(1'b1), .SUB(SUB[0]), .Carry_out(subtracao_1bit_1_carry_out));
  subtracao_1bit subtracao_1bit_2 (
    .A(A[1]), .B(B[1]), .Carry_in(subtracao_1bit_1_carry_out), .SUB(SUB[1]),
    .Carry_out(subtracao_1bit_2_carry_out));
  subtracao_1bit subtracao_1bit_3 (
    .A(A[2]), .B(B[2]), .Carry_in(subtracao_1bit_2_carry_out), .SUB(SUB[2]),
    .Carry_out(subtracao_1bit_3_carry_out));
  subtracao_1bit subtracao_1bit_4 (
    .A(A[3]), .B(B[3]), .Carry_in(subtracao_1bit_3_carry_out), .SUB(SUB[3]),
    .Carry_out(subtracao_1bit_4_carry_out));
  subtracao_1bit subtracao_1bit_5 (
    .A(A[4]), .B(B[4]), .Carry_in(subtracao_1bit_4_carry_out), .SUB(SUB[4]),
    .Carry_out(subtracao_1bit_5_carry_out));
  subtracao_1bit subtracao_1bit_6 (
    .A(A[5]), .B(B[5]), .Carry_in(subtracao_1bit_5_carry_out), .SUB(SUB[5]),
    .Carry_out(subtracao_1bit_6_carry_out));
  subtracao_1bit subtracao_1bit_7 (
    .A(A[6]), .B(B[6]), .Carry_in(subtracao_1bit_6_carry_out), .SUB(SUB[6]),
    .Carry_out(subtracao_1bit_7_carry_out));
  subtracao_1bit subtracao_1bit_8 (
    .A(A[7]), .B(B[7]), .Carry_in(subtracao_1bit_7_carry_out), .SUB(SUB[7]),
    .Carry_out(subtracao_1bit_8_carry_out));
  subtracao_1bit subtracao_1bit_9 (
    .A(A[8]), .B(B[8]), .Carry_in(subtracao_1bit_8_carry_out), .SUB(SUB[8]),
    .Carry_out(subtracao_1bit_9_carry_out));
  subtracao_1bit subtracao_1bit_10 (
    .A(A[9]), .B(B[9]), .Carry_in(subtracao_1bit_9_carry_out), .SUB(SUB[9]),
    .Carry_out(subtracao_1bit_10_carry_out));
  subtracao_1bit subtracao_1bit_11 (
    .A(A[10]), .B(B[10]), .Carry_in(subtracao_1bit_10_carry_out), .SUB(SUB[10]),
    .Carry_out(subtracao_1bit_11_carry_out));
  subtracao_1bit subtracao_1bit_12 (
    .A(A[11]), .B(B[11]), .Carry_in(subtracao_1bit_11_carry_out), .SUB(SUB[11]),
    .Carry_out(subtracao_1bit_12_carry_out));
  subtracao_1bit subtracao_1bit_13 (
    .A(A[12]), .B(B[12]), .Carry_in(subtracao_1bit_12_carry_out), .SUB(SUB[12]),
    .Carry_out(subtracao_1bit_13_carry_out));
  subtracao_1bit subtracao_1bit_14 (
    .A(A[13]), .B(B[13]), .Carry_in(subtracao_1bit_13_carry_out), .SUB(SUB[13]),
    .Carry_out(subtracao_1bit_14_carry_out));
  subtracao_1bit subtracao_1bit_15 (
    .A(A[14]), .B(B[14]), .Carry_in(subtracao_1bit_14_carry_out), .SUB(SUB[14]),
    .Carry_out(subtracao_1bit_15_carry_out));
  subtracao_1bit subtracao_1bit_16 (
    .A(A[15]), .B(B[15]), .Carry_in(subtracao_1bit_15_carry_out), .SUB(SUB[15]),
    .Carry_out(subtracao_1bit_16_carry_out));
  subtracao_1bit subtracao_1bit_17 (
    .A(A[16]), .B(B[16]), .Carry_in(subtracao_1bit_16_carry_out), .SUB(SUB[16]),
    .Carry_out(subtracao_1bit_17_carry_out));
  subtracao_1bit subtracao_1bit_18 (
    .A(A[17]), .B(B[17]), .Carry_in(subtracao_1bit_17_carry_out), .SUB(SUB[17]),
    .Carry_out(subtracao_1bit_18_carry_out));
  subtracao_1bit subtracao_1bit_19 (
    .A(A[18]), .B(B[18]), .Carry_in(subtracao_1bit_18_carry_out), .SUB(SUB[18]),
    .Carry_out(subtracao_1bit_19_carry_out));
  subtracao_1bit subtracao_1bit_20 (
    .A(A[19]), .B(B[19]), .Carry_in(subtracao_1bit_19_carry_out), .SUB(SUB[19]),
    .Carry_out(subtracao_1bit_20_carry_out));
  subtracao_1bit subtracao_1bit_21 (
    .A(A[20]), .B(B[20]), .Carry_in(subtracao_1bit_20_carry_out), .SUB(SUB[20]),
    .Carry_out(subtracao_1bit_21_carry_out));
  subtracao_1bit subtracao_1bit_22 (
    .A(A[21]), .B(B[21]), .Carry_in(subtracao_1bit_21_carry_out), .SUB(SUB[21]),
    .Carry_out(subtracao_1bit_22_carry_out));
  subtracao_1bit subtracao_1bit_23 (
    .A(A[22]), .B(B[22]), .Carry_in(subtracao_1bit_22_carry_out), .SUB(SUB[22]),
    .Carry_out(subtracao_1bit_23_carry_out));
  subtracao_1bit subtracao_1bit_24 (
    .A(A[23]), .B(B[23]), .Carry_in(subtracao_1bit_23_carry_out), .SUB(SUB[23]),
    .Carry_out(subtracao_1bit_24_carry_out));
  subtracao_1bit subtracao_1bit_25 (
    .A(A[24]), .B(B[24]), .Carry_in(subtracao_1bit_24_carry_out), .SUB(SUB[24]),
    .Carry_out(subtracao_1bit_25_carry_out));
  subtracao_1bit subtracao_1bit_26 (
    .A(A[25]), .B(B[25]), .Carry_in(subtracao_1bit_25_carry_out), .SUB(SUB[25]),
    .Carry_out(subtracao_1bit_26_carry_out));
  subtracao_1bit subtracao_1bit_27 (
    .A(A[26]), .B(B[26]), .Carry_in(subtracao_1bit_26_carry_out), .SUB(SUB[26]),
    .Carry_out(subtracao_1bit_27_carry_out));
  subtracao_1bit subtracao_1bit_28 (
    .A(A[27]), .B(B[27]), .Carry_in(subtracao_1bit_27_carry_out), .SUB(SUB[27]),
    .Carry_out(subtracao_1bit_28_carry_out));
  subtracao_1bit subtracao_1bit_29 (
    .A(A[28]), .B(B[28]), .Carry_in(subtracao_1bit_28_carry_out), .SUB(SUB[28]),
    .Carry_out(subtracao_1bit_29_carry_out));
  subtracao_1bit subtracao_1bit_30 (
    .A(A[29]), .B(B[29]), .Carry_in(subtracao_1bit_29_carry_out), .SUB(SUB[29]),
    .Carry_out(subtracao_1bit_30_carry_out));
  subtracao_1bit subtracao_1bit_31 (
    .A(A[30]), .B(B[30]), .Carry_in(subtracao_1bit_30_carry_out), .SUB(SUB[30]),
    .Carry_out(subtracao_1bit_31_carry_out));
  subtracao_1bit subtracao_1bit_32 (
    .A(A[31]), .B(B[31]), .Carry_in(subtracao_1bit_31_carry_out), .SUB(SUB[31]),
    .Carry_out(subtracao_1bit_32_carry_out));
  not not_1 (Negativo, subtracao_1bit_32_carry_out);
  xor xor_1 (Overflow, subtracao_1bit_32_carry_out, subtracao_1bit_31_carry_out);
endmodule

module slt (
  input  [31:0] A,
  input  [31:0] B,
  output [31:0] S
);

  wire subtracao_32bit_1_negativo;

  subtracao_32bit subtracao_32bit_1 (.B(B), .A(A), .Negativo(subtracao_32bit_1_negativo));  // open: SUB, Overflow
  assign S = {{31{1'b0}}, subtracao_32bit_1_negativo};  // Bit_Extender bit_extender_1

  // Notes on the sheet:
  //   1 para A<B
endmodule

module main (
  input  [31:0] in_1,
  input  [31:0] B,
  input  [3:0] AluOp,
  output [31:0] out_4,
  output out_5
);

  ULA ula_1 (.A(in_1), .B(B), .AluOp(AluOp), .Result(out_4), .Zero(out_5));
endmodule

module bloco_artmetico (
  input  [31:0] A,
  input  [31:0] B,
  input  [3:0] AluOp,
  output [31:0] S
);

  wire [31:0] adicao_32bit_1_sum, and_1_out, and_2_out, and_3_out, bit_extender_1_out, bit_extender_2_out,
       bit_extender_3_out, bit_extender_4_out, slt_1_s, subtracao_32bit_1_sub;

  adicao_32bit adicao_32bit_1 (.B(B), .A(A), .SUM(adicao_32bit_1_sum));  // open: Overflow
  subtracao_32bit subtracao_32bit_1 (.B(B), .A(A), .SUB(subtracao_32bit_1_sub));  // open: Negativo, Overflow
  slt slt_1 (.A(A), .B(B), .S(slt_1_s));
  assign bit_extender_1_out = {{31{AluOp[0]}}, AluOp[0]};  // Bit_Extender bit_extender_1
  assign bit_extender_2_out = {{31{AluOp[1]}}, AluOp[1]};  // Bit_Extender bit_extender_2
  assign bit_extender_3_out = {{31{AluOp[2]}}, AluOp[2]};  // Bit_Extender bit_extender_3
  assign bit_extender_4_out = {{31{AluOp[3]}}, AluOp[3]};  // Bit_Extender bit_extender_4
  assign and_1_out = adicao_32bit_1_sum & ~bit_extender_1_out & ~bit_extender_2_out & ~bit_extender_3_out & ~bit_extender_4_out;  // AND_Gate and_1, 32 bits wide
  assign and_2_out = subtracao_32bit_1_sub & ~bit_extender_1_out & bit_extender_2_out & ~bit_extender_3_out & ~bit_extender_4_out;  // AND_Gate and_2, 32 bits wide
  assign and_3_out = slt_1_s & ~bit_extender_1_out & bit_extender_2_out & ~bit_extender_3_out & bit_extender_4_out;  // AND_Gate and_3, 32 bits wide
  assign S = and_1_out | and_2_out | and_3_out;  // OR_Gate or_1, 32 bits wide

  // Notes on the sheet:
  //   Entradas de A e B de 0 a 31
  //   <-Bit MSB à esquerda<-
  //   ->Bit LSB à direita->
  //   Full adder = 0000
  //   Subtrator = 0010
  //   Slt = 1010
  //   S3 S2 S1 S
  //   Seletor de entradas
endmodule

module ULA (
  input  [31:0] A,
  input  [31:0] B,
  input  [3:0] AluOp,
  output [31:0] Result,
  output Zero
);

  wire [31:0] and_1_out, and_2_out, bit_extender_1_out, bloco_artmetico_1_s, bloco_logico_1_s;

  bloco_artmetico bloco_artmetico_1 (.A(A), .B(B), .AluOp(AluOp), .S(bloco_artmetico_1_s));
  bloco_logico bloco_logico_1 (.A(A), .B(B), .AluOp(AluOp), .S(bloco_logico_1_s));
  assign bit_extender_1_out = {{31{AluOp[2]}}, AluOp[2]};  // Bit_Extender bit_extender_1
  assign and_1_out = bloco_artmetico_1_s & ~bit_extender_1_out;  // AND_Gate and_1, 32 bits wide
  assign and_2_out = bloco_logico_1_s & bit_extender_1_out;  // AND_Gate and_2, 32 bits wide
  assign Result = and_1_out | and_2_out;  // OR_Gate or_1, 32 bits wide
  detector_de_zeros detector_de_zeros_1 (.Z(Result), .R(Zero));

  // Notes on the sheet:
  //   Entradas A e B
  //   Seletor de saída
  //   Resultado da operação
  //   resulta 1 caso todos os bits de Result 
  //   sejam bits 0's
  //   Detector de zero 
endmodule

module And_32_bits_splitter (
  input  [31:0] A,
  input  [31:0] B,
  output [31:0] S
);

  assign S = A & B;  // AND_Gate and_1, 32 bits wide
endmodule

module porta_nor_32_bits_splitter (
  input  [31:0] A,
  input  [31:0] B,
  output [31:0] S
);

  assign S = ~(A | B);  // NOR_Gate nor_1, 32 bits wide
endmodule

module porta_or_32_bits_splitter (
  input  [31:0] A,
  input  [31:0] B,
  output [31:0] S
);

  assign S = A | B;  // OR_Gate or_1, 32 bits wide
endmodule

module porta_xor_32_bits_splitter (
  input  [31:0] A,
  input  [31:0] B,
  output [31:0] S
);

  assign S = A ^ B;  // XOR_Gate xor_1, 32 bits wide
endmodule

module porta_xor_32bits (
  input  [31:0] A,
  input  [31:0] B,
  output [31:0] S
);

  assign S = A ^ B;  // XOR_Gate xor_1, 32 bits wide
endmodule

module bloco_logico (
  input  [31:0] A,
  input  [31:0] B,
  input  [3:0] AluOp,
  output [31:0] S
);

  wire [31:0] and_1_out, and_2_out, and_3_out, and_4_out, and_32_bits_splitter_1_s, bit_extender_1_out,
       bit_extender_2_out, bit_extender_3_out, bit_extender_4_out, porta_nor_32_bits_splitter_1_s,
       porta_or_32_bits_splitter_1_s, porta_xor_32_bits_splitter_1_s;

  And_32_bits_splitter and_32_bits_splitter_1 (.A(A), .B(B), .S(and_32_bits_splitter_1_s));
  porta_or_32_bits_splitter porta_or_32_bits_splitter_1 (.A(A), .B(B), .S(porta_or_32_bits_splitter_1_s));
  porta_xor_32_bits_splitter porta_xor_32_bits_splitter_1 (.A(A), .B(B), .S(porta_xor_32_bits_splitter_1_s));
  porta_nor_32_bits_splitter porta_nor_32_bits_splitter_1 (.A(A), .B(B), .S(porta_nor_32_bits_splitter_1_s));
  assign bit_extender_1_out = {{31{AluOp[3]}}, AluOp[3]};  // Bit_Extender bit_extender_1
  assign bit_extender_2_out = {{31{AluOp[2]}}, AluOp[2]};  // Bit_Extender bit_extender_2
  assign and_1_out = and_32_bits_splitter_1_s & ~bit_extender_1_out & bit_extender_2_out & ~bit_extender_3_out & ~bit_extender_4_out;  // AND_Gate and_1, 32 bits wide
  assign and_2_out = porta_or_32_bits_splitter_1_s & ~bit_extender_1_out & bit_extender_2_out & ~bit_extender_3_out & bit_extender_4_out;  // AND_Gate and_2, 32 bits wide
  assign and_3_out = porta_xor_32_bits_splitter_1_s & ~bit_extender_1_out & bit_extender_2_out & bit_extender_3_out & ~bit_extender_4_out;  // AND_Gate and_3, 32 bits wide
  assign and_4_out = porta_nor_32_bits_splitter_1_s & ~bit_extender_1_out & bit_extender_2_out & bit_extender_3_out & bit_extender_4_out;  // AND_Gate and_4, 32 bits wide
  assign bit_extender_3_out = {{31{AluOp[1]}}, AluOp[1]};  // Bit_Extender bit_extender_3
  assign bit_extender_4_out = {{31{AluOp[0]}}, AluOp[0]};  // Bit_Extender bit_extender_4
  assign S = and_1_out | and_2_out | and_3_out | and_4_out;  // OR_Gate or_1, 32 bits wide

  // Notes on the sheet:
  //   Entradas de A e B de 0 a 31
  //   <-Bit MSB à esquerda<-
  //   ->Bit LSB à direita->
  //   Bloco Lógico 
  //   operações lógicas
  //   and =0100
  //   or = 0101
  //   xor = 0110
  //   nor =0111
  //   S3 S2 S1 S
  //   seletor de entradas
  //   Saída do bitwise
endmodule

module detector_de_zeros (
  input  [31:0] Z,
  output R
);

  wire or_1_out;

  or or_1 (or_1_out, Z[31], Z[30], Z[29], Z[28], Z[27], Z[26], Z[25], Z[24], Z[23], Z[22], Z[21], Z[20], Z[19], Z[18], Z[17], Z[16], Z[15], Z[14], Z[13], Z[12], Z[11], Z[10], Z[9], Z[8], Z[7], Z[6], Z[5], Z[4], Z[3], Z[2], Z[1], Z[0]);
  not not_1 (R, or_1_out);

  // Notes on the sheet:
  //   Detector de zeros
endmodule
