// Logisim project Trabalho_logica_digital.circ as structural Verilog: 16 circuits, main circuit main
module adicao_1bit (
  input  A,
  input  B,
  input  Carry_in,
  output SUM,
  output Carry_out
);

  wire and_1_out, and_2_out, xor_1_out;

  xor xor_1 (xor_1_out, B, A);
  and and_1 (and_1_out, B, A);
  xor xor_2 (SUM, xor_1_out, Carry_in);
  and and_2 (and_2_out, xor_1_out, Carry_in);
  or or_1 (Carry_out, and_2_out, and_1_out);
endmodule

module adicao_32bit (
  input  [31:0] A,
  input  [31:0] B,
  output [31:0] SUM,
  output Overflow
);

  wire adicao_1bit_1_carry_out, adicao_1bit_2_carry_out, adicao_1bit_3_carry_out, adicao_1bit_4_carry_out,
       adicao_1bit_5_carry_out, adicao_1bit_6_carry_out, adicao_1bit_7_carry_out, adicao_1bit_8_carry_out,
       adicao_1bit_9_carry_out, adicao_1bit_10_carry_out, adicao_1bit_11_carry_out, adicao_1bit_12_carry_out,
       adicao_1bit_13_carry_out, adicao_1bit_14_carry_out, adicao_1bit_15_carry_out,
       adicao_1bit_16_carry_out, adicao_1bit_17_carry_out, adicao_1bit_18_carry_out,
       adicao_1bit_19_carry_out, adicao_1bit_20_carry_out, adicao_1bit_21_carry_out,
       adicao_1bit_22_carry_out, adicao_1bit_23_carry_out, adicao_1bit_24_carry_out,
       adicao_1bit_25_carry_out, adicao_1bit_26_carry_out, adicao_1bit_27_carry_out,
       adicao_1bit_28_carry_out, adicao_1bit_29_carry_out, adicao_1bit_30_carry_out, adicao_1bit_31_carry_out;

  adicao_1bit adicao_1bit_1 (.Carry_in(1'b0), .A(A[0]), .B(B[0]), .SUM(SUM[0]), .Carry_out(adicao_1bit_1_carry_out));
  adicao_1bit adicao_1bit_2 (
    .Carry_in(adicao_1bit_1_carry_out), .A(A[1]), .B(B[1]), .SUM(SUM[1]), .Carry_out(adicao_1bit_2_carry_out));
  adicao_1bit adicao_1bit_3 (
    .Carry_in(adicao_1bit_2_carry_out), .A(A[2]), .B(B[2]), .SUM(SUM[2]), .Carry_out(adicao_1bit_3_carry_out));
  adicao_1bit adicao_1bit_4 (
    .Carry_in(adicao_1bit_3_carry_out), .A(A[3]), .B(B[3]), .SUM(SUM[3]), .Carry_out(adicao_1bit_4_carry_out));
  adicao_1bit adicao_1bit_5 (
    .Carry_in(adicao_1bit_4_carry_out), .A(A[4]), .B(B[4]), .SUM(SUM[4]), .Carry_out(adicao_1bit_5_carry_out));
  adicao_1bit adicao_1bit_6 (
    .Carry_in(adicao_1bit_5_carry_out), .A(A[5]), .B(B[5]), .SUM(SUM[5]), .Carry_out(adicao_1bit_6_carry_out));
  adicao_1bit adicao_1bit_7 (
    .Carry_in(adicao_1bit_6_carry_out), .A(A[6]), .B(B[6]), .SUM(SUM[6]), .Carry_out(adicao_1bit_7_carry_out));
  adicao_1bit adicao_1bit_8 (
    .Carry_in(adicao_1bit_7_carry_out), .A(A[7]), .B(B[7]), .SUM(SUM[7]), .Carry_out(adicao_1bit_8_carry_out));
  adicao_1bit adicao_1bit_9 (
    .Carry_in(adicao_1bit_8_carry_out), .A(A[8]), .B(B[8]), .SUM(SUM[8]), .Carry_out(adicao_1bit_9_carry_out));
  adicao_1bit adicao_1bit_10 (
    .Carry_in(adicao_1bit_9_carry_out), .A(A[9]), .B(B[9]), .SUM(SUM[9]), .Carry_out(adicao_1bit_10_carry_out));
  adicao_1bit adicao_1bit_11 (
    .Carry_in(adicao_1bit_10_carry_out), .A(A[10]), .B(B[10]), .SUM(SUM[10]),
    .Carry_out(adicao_1bit_11_carry_out));
  adicao_1bit adicao_1bit_12 (
    .Carry_in(adicao_1bit_11_carry_out), .A(A[11]), .B(B[11]), .SUM(SUM[11]),
    .Carry_out(adicao_1bit_12_carry_out));
  adicao_1bit adicao_1bit_13 (
    .Carry_in(adicao_1bit_12_carry_out), .A(A[12]), .B(B[12]), .SUM(SUM[12]),
    .Carry_out(adicao_1bit_13_carry_out));
  adicao_1bit adicao_1bit_14 (
    .Carry_in(adicao_1bit_13_carry_out), .A(A[13]), .B(B[13]), .SUM(SUM[13]),
    .Carry_out(adicao_1bit_14_carry_out));
  adicao_1bit adicao_1bit_15 (
    .Carry_in(adicao_1bit_14_carry_out), .A(A[14]), .B(B[14]), .SUM(SUM[14]),
    .Carry_out(adicao_1bit_15_carry_out));
  adicao_1bit adicao_1bit_16 (
    .Carry_in(adicao_1bit_15_carry_out), .A(A[15]), .B(B[15]), .SUM(SUM[15]),
    .Carry_out(adicao_1bit_16_carry_out));
  adicao_1bit adicao_1bit_17 (
    .Carry_in(adicao_1bit_16_carry_out), .A(A[16]), .B(B[16]), .SUM(SUM[16]),
    .Carry_out(adicao_1bit_17_carry_out));
  adicao_1bit adicao_1bit_18 (
    .Carry_in(adicao_1bit_17_carry_out), .A(A[17]), .B(B[17]), .SUM(SUM[17]),
    .Carry_out(adicao_1bit_18_carry_out));
  adicao_1bit adicao_1bit_19 (
    .Carry_in(adicao_1bit_18_carry_out), .A(A[18]), .B(B[18]), .SUM(SUM[18]),
    .Carry_out(adicao_1bit_19_carry_out));
  adicao_1bit adicao_1bit_20 (
    .Carry_in(adicao_1bit_19_carry_out), .A(A[19]), .B(B[19]), .SUM(SUM[19]),
    .Carry_out(adicao_1bit_20_carry_out));
  adicao_1bit adicao_1bit_21 (
    .Carry_in(adicao_1bit_20_carry_out), .A(A[20]), .B(B[20]), .SUM(SUM[20]),
    .Carry_out(adicao_1bit_21_carry_out));
  adicao_1bit adicao_1bit_22 (
    .Carry_in(adicao_1bit_21_carry_out), .A(A[21]), .B(B[21]), .SUM(SUM[21]),
    .Carry_out(adicao_1bit_22_carry_out));
  adicao_1bit adicao_1bit_23 (
    .Carry_in(adicao_1bit_22_carry_out), .A(A[22]), .B(B[22]), .SUM(SUM[22]),
    .Carry_out(adicao_1bit_23_carry_out));
  adicao_1bit adicao_1bit_24 (
    .Carry_in(adicao_1bit_23_carry_out), .A(A[23]), .B(B[23]), .SUM(SUM[23]),
    .Carry_out(adicao_1bit_24_carry_out));
  adicao_1bit adicao_1bit_25 (
    .Carry_in(adicao_1bit_24_carry_out), .A(A[24]), .B(B[24]), .SUM(SUM[24]),
    .Carry_out(adicao_1bit_25_carry_out));
  adicao_1bit adicao_1bit_26 (
    .Carry_in(adicao_1bit_25_carry_out), .A(A[25]), .B(B[25]), .SUM(SUM[25]),
    .Carry_out(adicao_1bit_26_carry_out));
  adicao_1bit adicao_1bit_27 (
    .Carry_in(adicao_1bit_26_carry_out), .A(A[26]), .B(B[26]), .SUM(SUM[26]),
    .Carry_out(adicao_1bit_27_carry_out));
  adicao_1bit adicao_1bit_28 (
    .Carry_in(adicao_1bit_27_carry_out), .A(A[27]), .B(B[27]), .SUM(SUM[27]),
    .Carry_out(adicao_1bit_28_carry_out));
  adicao_1bit adicao_1bit_29 (
    .Carry_in(adicao_1bit_28_carry_out), .A(A[28]), .B(B[28]), .SUM(SUM[28]),
    .Carry_out(adicao_1bit_29_carry_out));
  adicao_1bit adicao_1bit_30 (
    .Carry_in(adicao_1bit_29_carry_out), .A(A[29]), .B(B[29]), .SUM(SUM[29]),
    .Carry_out(adicao_1bit_30_carry_out));
  adicao_1bit adicao_1bit_31 (
    .Carry_in(adicao_1bit_30_carry_out), .A(A[30]), .B(B[30]), .SUM(SUM[30]),
    .Carry_out(adicao_1bit_31_carry_out));
  adicao_1bit adicao_1bit_32 (
    .Carry_in(adicao_1bit_31_carry_out), .A(A[31]), .B(B[31]), .SUM(SUM[31]), .Carry_out(Overflow));
endmodule

module subtracao_1bit (
  input  A,
  input  B,
  input  Carry_in,
  output SUB,
  output Carry_out
);

  wire not_1_out;

  not not_1 (not_1_out, B);
  adicao_1bit adicao_1bit_1 (.Carry_in(Carry_in), .A(A), .B(not_1_out), .SUM(SUB), .Carry_out(Carry_out));
endmodule

module subtracao_32bit (
  input  [31:0] A,
  input  [31:0] B,
  output [31:0] SUB,
  output Negativo,
  output Overflow
);

  wire subtracao_1bit_1_carry_out, subtracao_1bit_2_carry_out, subtracao_1bit_3_carry_out,
       subtracao_1bit_4_carry_out, subtracao_1bit_5_carry_out, subtracao_1bit_6_carry_out,
       subtracao_1bit_7_carry_out, subtracao_1bit_8_carry_out, subtracao_1bit_9_carry_out,
       subtracao_1bit_10_carry_out, subtracao_1bit_11_carry_out, subtracao_1bit_12_carry_out,
       subtracao_1bit_13_carry_out, subtracao_1bit_14_carry_out, subtracao_1bit_15_carry_out,
       subtracao_1bit_16_carry_out, subtracao_1bit_17_carry_out, subtracao_1bit_18_carry_out,
       subtracao_1bit_19_carry_out, subtracao_1bit_20_carry_out, subtracao_1bit_21_carry_out,
       subtracao_1bit_22_carry_out, subtracao_1bit_23_carry_out, subtracao_1bit_24_carry_out,
       subtracao_1bit_25_carry_out, subtracao_1bit_26_carry_out, subtracao_1bit_27_carry_out,
       subtracao_1bit_28_carry_out, subtracao_1bit_29_carry_out, subtracao_1bit_30_carry_out,
       subtracao_1bit_31_carry_out, subtracao_1bit_32_carry_out;

  subtracao_1bit subtracao_1bit_1 (
    .A(A[0]), .B(B[0]), .Carry_in(1'b1), .SUB(SUB[0]), .Carry_out(subtracao_1bit_1_carry_out));
  subtracao_1bit subtracao_1bit_2 (
    .A(A[1]), .B(B[1]), .Carry_in(subtracao_1bit_1_carry_out), .SUB(SUB[1]),
    .Carry_out(subtracao_1bit_2_carry_out));
  subtracao_1bit subtracao_1bit_3 (
    .A(A[2]), .B(B[2]), .Carry_in(subtracao_1bit_2_carry_out), .SUB(SUB[2]),
    .Carry_out(subtracao_1bit_3_carry_out));
  subtracao_1bit subtracao_1bit_4 (
    .A(A[3]), .B(B[3]), .Carry_in(subtracao_1bit_3_carry_out), .SUB(SUB[3]),
    .Carry_out(subtracao_1bit_4_carry_out));
  subtracao_1bit subtracao_1bit_5 (
    .A(A[4]), .B(B[4]), .Carry_in(subtracao_1bit_4_carry_out), .SUB(SUB[4]),
    .Carry_out(subtracao_1bit_5_carry_out));
  subtracao_1bit subtracao_1bit_6 (
    .A(A[5]), .B(B[5]), .Carry_in(subtracao_1bit_5_carry_out), .SUB(SUB[5]),
    .Carry_out(subtracao_1bit_6_carry_out));
  subtracao_1bit subtracao_1bit_7 (
    .A(A[6]), .B(B[6]), .Carry_in(subtracao_1bit_6_carry_out), .SUB(SUB[6]),
    .Carry_out(subtracao_1bit_7_carry_out));
  subtracao_1bit subtracao_1bit_8 (
    .A(A[7]), .B(B[7]), .Carry_in(subtracao_1bit_7_carry_out), .SUB(SUB[7]),
    .Carry_out(subtracao_1bit_8_carry_out));
  subtracao_1bit subtracao_1bit_9 (
    .A(A[8]), .B(B[8]), .Carry_in(subtracao_1bit_8_carry_out), .SUB(SUB[8]),
    .Carry_out(subtracao_1bit_9_carry_out));
  subtracao_1bit subtracao_1bit_10 (
    .A(A[9]), .B(B[9]), .Carry_in(subtracao_1bit_9_carry_out), .SUB(SUB[9]),
    .Carry_out(subtracao_1bit_10_carry_out));
  subtracao_1bit subtracao_1bit_11 (
    .A(A[10]), .B(B[10]), .Carry_in(subtracao_1bit_10_carry_out), .SUB(SUB[10]),
    .Carry_out(subtracao_1bit_11_carry_out));
  subtracao_1bit subtracao_1bit_12 (
    .A(A[11]), .B(B[11]), .Carry_in(subtracao_1bit_11_carry_out), .SUB(SUB[11]),
    .Carry_out(subtracao_1bit_12_carry_out));
  subtracao_1bit subtracao_1bit_13 (
    .A(A[12]), .B(B[12]), .Carry_in(subtracao_1bit_12_carry_out), .SUB(SUB[12]),
    .Carry_out(subtracao_1bit_13_carry_out));
  subtracao_1bit subtracao_1bit_14 (
    .A(A[13]), .B(B[13]), .Carry_in(subtracao_1bit_13_carry_out), .SUB(SUB[13]),
    .Carry_out(subtracao_1bit_14_carry_out));
  subtracao_1bit subtracao_1bit_15 (
    .A(A[14]), .B(B[14]), .Carry_in(subtracao_1bit_14_carry_out), .SUB(SUB[14]),
    .Carry_out(subtracao_1bit_15_carry_out));
  subtracao_1bit subtracao_1bit_16 (
    .A(A[15]), .B(B[15]), .Carry_in(subtracao_1bit_15_carry_out), .SUB(SUB[15]),
    .Carry_out(subtracao_1bit_16_carry_out));
  subtracao_1bit subtracao_1bit_17 (
    .A(A[16]), .B(B[16]), .Carry_in(subtracao_1bit_16_carry_out), .SUB(SUB[16]),
    .Carry_out(subtracao_1bit_17_carry_out));
  subtracao_1bit subtracao_1bit_18 (
    .A(A[17]), .B(B[17]), .Carry_in(subtracao_1bit_17_carry_out), .SUB(SUB[17]),
    .Carry_out(subtracao_1bit_18_carry_out));
  subtracao_1bit subtracao_1bit_19 (
    .A(A[18]), .B(B[18]), .Carry_in(subtracao_1bit_18_carry_out), .SUB(SUB[18]),
    .Carry_out(subtracao_1bit_19_carry_out));
  subtracao_1bit subtracao_1bit_20 (
    .A(A[19]), .B(B[19]), .Carry_in(subtracao_1bit_19_carry_out), .SUB(SUB[19]),
    .Carry_out(subtracao_1bit_20_carry_out));
  subtracao_1bit subtracao_1bit_21 (
    .A(A[20]), .B(B[20]), .Carry_in(subtracao_1bit_20_carry_out), .SUB(SUB[20]),
    .Carry_out(subtracao_1bit_21_carry_out));
  subtracao_1bit subtracao_1bit_22 (
    .A(A[21]), .B(B[21]), .Carry_in(subtracao_1bit_21_carry_out), .SUB(SUB[21]),
    .Carry_out(subtracao_1bit_22_carry_out));
  subtracao_1bit subtracao_1bit_23 (
    .A(A[22]), .B(B[22]), .Carry_in(subtracao_1bit_22_carry_out), .SUB(SUB[22]),
    .Carry_out(subtracao_1bit_23_carry_out));
  subtracao_1bit subtracao_1bit_24 (
    .A(A[23]), .B(B[23]), .Carry_in(subtracao_1bit_23_carry_out), .SUB(SUB[23]),
    .Carry_out(subtracao_1bit_24_carry_out));
  subtracao_1bit subtracao_1bit_25 (
    .A(A[24]), .B(B[24]), .Carry_in(subtracao_1bit_24_carry_out), .SUB(SUB[24]),
    .Carry_out(subtracao_1bit_25_carry_out));
  subtracao_1bit subtracao_1bit_26 (
    .A(A[25]), .B(B[25]), .Carry_in(subtracao_1bit_25_carry_out), .SUB(SUB[25]),
    .Carry_out(subtracao_1bit_26_carry_out));
  subtracao_1bit subtracao_1bit_27 (
    .A(A[26]), .B(B[26]), .Carry_in(subtracao_1bit_26_carry_out), .SUB(SUB[26]),
    .Carry_out(subtracao_1bit_27_carry_out));
  subtracao_1bit subtracao_1bit_28 (
    .A(A[27]), .B(B[27]), .Carry_in(subtracao_1bit_27_carry_out), .SUB(SUB[27]),
    .Carry_out(subtracao_1bit_28_carry_out));
  subtracao_1bit subtracao_1bit_29 (
    .A(A[28]), .B(B[28]), .Carry_in(subtracao_1bit_28_carry_out), .SUB(SUB[28]),
    .Carry_out(subtracao_1bit_29_carry_out));
  subtracao_1bit subtracao_1bit_30 (
    .A(A[29]), .B(B[29]), .Carry_in(subtracao_1bit_29_carry_out), .SUB(SUB[29]),
    .Carry_out(subtracao_1bit_30_carry_out));
  subtracao_1bit subtracao_1bit_31 (
    .A(A[30]), .B(B[30]), .Carry_in(subtracao_1bit_30_carry_out), .SUB(SUB[30]),
    .Carry_out(subtracao_1bit_31_carry_out));
  subtracao_1bit subtracao_1bit_32 (
    .A(A[31]), .B(B[31]), .Carry_in(subtracao_1bit_31_carry_out), .SUB(SUB[31]),
    .Carry_out(subtracao_1bit_32_carry_out));
  not not_1 (Negativo, subtracao_1bit_32_carry_out);
  xor xor_1 (Overflow, subtracao_1bit_32_carry_out, subtracao_1bit_31_carry_out);
endmodule

module slt (
  input  [31:0] A,
  input  [31:0] B,
  output [31:0] S
);

  wire subtracao_32bit_1_negativo;

  subtracao_32bit subtracao_32bit_1 (.B(B), .A(A), .Negativo(subtracao_32bit_1_negativo));  // open: SUB, Overflow
  assign S = {{31{1'b0}}, subtracao_32bit_1_negativo};  // Bit_Extender bit_extender_1

  // Notes on the sheet:
  //   1 para A<B
endmodule

module main (
  input  [31:0] in_1,
  input  [31:0] B,
  input  [3:0] AluOp,
  output [31:0] out_4,
  output out_5
);

  ula ula_1 (.A(in_1), .B(B), .AluOp(AluOp), .Result(out_4));
endmodule

module bloco_artmetico (
  input  [31:0] A,
  input  [31:0] B,
  input  [3:0] AluOp,
  output [31:0] S
);

  wire [31:0] adicao_32bit_1_sum, and_1_out, and_2_out, and_3_out, bit_extender_1_out, bit_extender_2_out,
       bit_extender_3_out, bit_extender_4_out, slt_1_s, subtracao_32bit_1_sub;

  adicao_32bit adicao_32bit_1 (.B(B), .A(A), .SUM(adicao_32bit_1_sum));  // open: Overflow
  subtracao_32bit subtracao_32bit_1 (.B(B), .A(A), .SUB(subtracao_32bit_1_sub));  // open: Negativo, Overflow
  slt slt_1 (.A(A), .B(B), .S(slt_1_s));
  assign bit_extender_1_out = {{31{AluOp[0]}}, AluOp[0]};  // Bit_Extender bit_extender_1
  assign bit_extender_2_out = {{31{AluOp[1]}}, AluOp[1]};  // Bit_Extender bit_extender_2
  assign bit_extender_3_out = {{31{AluOp[2]}}, AluOp[2]};  // Bit_Extender bit_extender_3
  assign bit_extender_4_out = {{31{AluOp[3]}}, AluOp[3]};  // Bit_Extender bit_extender_4
  assign and_1_out = adicao_32bit_1_sum & ~bit_extender_1_out & ~bit_extender_2_out & ~bit_extender_3_out & ~bit_extender_4_out;  // AND_Gate and_1, 32 bits wide
  assign and_2_out = subtracao_32bit_1_sub & ~bit_extender_1_out & bit_extender_2_out & ~bit_extender_3_out & ~bit_extender_4_out;  // AND_Gate and_2, 32 bits wide
  assign and_3_out = slt_1_s & ~bit_extender_1_out & bit_extender_2_out & ~bit_extender_3_out & bit_extender_4_out;  // AND_Gate and_3, 32 bits wide
  assign S = and_1_out | and_2_out | and_3_out;  // OR_Gate or_1, 32 bits wide
endmodule

module ula (
  input  [31:0] A,
  input  [31:0] B,
  input  [3:0] AluOp,
  output [31:0] Result
);

  wire [31:0] and_1_out, and_2_out, bit_extender_1_out, bloco_artmetico_1_s, bloco_logico_1_s;

  bloco_artmetico bloco_artmetico_1 (.A(A), .B(B), .AluOp(AluOp), .S(bloco_artmetico_1_s));
  bloco_logico bloco_logico_1 (.A(A), .B(B), .AluOp(AluOp), .S(bloco_logico_1_s));
  assign bit_extender_1_out = {{31{AluOp[2]}}, AluOp[2]};  // Bit_Extender bit_extender_1
  assign and_1_out = bloco_artmetico_1_s & ~bit_extender_1_out;  // AND_Gate and_1, 32 bits wide
  assign and_2_out = bloco_logico_1_s & bit_extender_1_out;  // AND_Gate and_2, 32 bits wide
  assign Result = and_1_out | and_2_out;  // OR_Gate or_1, 32 bits wide
endmodule

module And4bits (
  input  A,
  input  B,
  input  A_1,
  input  B_1,
  input  A_2,
  input  B_2,
  input  A_3,
  input  B_3,
  output S,
  output S_1,
  output S_2,
  output S_3
);

  and and_1 (S, A, B);
  and and_2 (S_1, A_1, B_1);
  and and_3 (S_2, A_2, B_2);
  and and_4 (S_3, A_3, B_3);
endmodule

module AND_32_BITS (
  input  A,
  input  B,
  input  A_1,
  input  B_1,
  input  A_2,
  input  B_2,
  input  A_3,
  input  B_3,
  input  A_4,
  input  B_4,
  input  A_5,
  input  B_5,
  input  A_6,
  input  B_6,
  input  A_7,
  input  B_7,
  input  A_8,
  input  B_8,
  input  A_9,
  input  B_9,
  input  A_10,
  input  B_10,
  input  A_11,
  input  B_11,
  input  A_12,
  input  B_12,
  input  A_13,
  input  B_13,
  input  A_14,
  input  B_14,
  input  A_15,
  input  B_15,
  input  A_16,
  input  B_16,
  input  A_17,
  input  B_17,
  input  A_18,
  input  B_18,
  input  A_19,
  input  B_19,
  input  A_20,
  input  B_20,
  input  A_21,
  input  B_21,
  input  A_22,
  input  B_22,
  input  A_23,
  input  B_23,
  input  A_24,
  input  B_24,
  input  A_25,
  input  B_25,
  input  A_26,
  input  B_26,
  input  A_27,
  input  B_27,
  input  A_28,
  input  B_28,
  input  A_29,
  input  B_29,
  input  A_30,
  input  B_30,
  input  A_31,
  input  B_31,
  output [31:0] out_65
);

  And4bits and4bits_1 (
    .B(B), .A_1(A_1), .B_1(B_1), .A_2(A_2), .B_2(B_2), .A_3(A_3), .B_3(B_3), .A(A), .S(out_65[0]),
    .S_1(out_65[1]), .S_2(out_65[2]), .S_3(out_65[3]));
  And4bits and4bits_2 (
    .B(B_4), .A_1(A_5), .B_1(B_5), .A_2(A_6), .B_2(B_6), .A_3(A_7), .B_3(B_7), .A(A_4), .S(out_65[4]),
    .S_1(out_65[5]), .S_2(out_65[6]), .S_3(out_65[7]));
  And4bits and4bits_3 (
    .B(B_8), .A_1(A_9), .B_1(B_9), .A_2(A_10), .B_2(B_10), .A_3(A_11), .B_3(B_11), .A(A_8), .S(out_65[8]),
    .S_1(out_65[9]), .S_2(out_65[10]), .S_3(out_65[11]));
  And4bits and4bits_4 (
    .B(B_12), .A_1(A_13), .B_1(B_13), .A_2(A_14), .B_2(B_14), .A_3(A_15), .B_3(B_15), .A(A_12),
    .S(out_65[12]), .S_1(out_65[13]), .S_2(out_65[14]), .S_3(out_65[15]));
  And4bits and4bits_5 (
    .B(B_16), .A_1(A_17), .B_1(B_17), .A_2(A_18), .B_2(B_18), .A_3(A_19), .B_3(B_19), .A(A_16),
    .S(out_65[16]), .S_1(out_65[17]), .S_2(out_65[18]), .S_3(out_65[19]));
  And4bits and4bits_6 (
    .B(B_20), .A_1(A_21), .B_1(B_21), .A_2(A_22), .B_2(B_22), .A_3(A_23), .B_3(B_23), .A(A_20),
    .S(out_65[20]), .S_1(out_65[21]), .S_2(out_65[22]), .S_3(out_65[23]));
  And4bits and4bits_7 (
    .B(B_24), .A_1(A_25), .B_1(B_25), .A_2(A_26), .B_2(B_26), .A_3(A_27), .B_3(B_27), .A(A_24),
    .S(out_65[24]), .S_1(out_65[25]), .S_2(out_65[26]), .S_3(out_65[27]));
  And4bits and4bits_8 (
    .B(B_28), .A_1(A_29), .B_1(B_29), .A_2(A_30), .B_2(B_30), .A_3(A_31), .B_3(B_31), .A(A_28),
    .S(out_65[28]), .S_1(out_65[29]), .S_2(out_65[30]), .S_3(out_65[31]));
endmodule

module And_32_bits_splitter (
  input  [31:0] A,
  input  [31:0] B,
  output [31:0] S
);

  assign S = A & B;  // AND_Gate and_1, 32 bits wide
endmodule

module porta_nor_32_bits_splitter (
  input  [31:0] A,
  input  [31:0] B,
  output [31:0] S
);

  assign S = ~(A | B);  // NOR_Gate nor_1, 32 bits wide
endmodule

module porta_or_32_bits_splitter (
  input  [31:0] A,
  input  [31:0] B,
  output [31:0] S
);

  assign S = A | B;  // OR_Gate or_1, 32 bits wide
endmodule

module porta_xor_32_bits_splitter (
  input  [31:0] A,
  input  [31:0] B,
  output [31:0] S
);

  assign S = A ^ B;  // XOR_Gate xor_1, 32 bits wide
endmodule

module porta_xor_32bits (
  input  [31:0] A,
  input  [31:0] B,
  output [31:0] S
);

  assign S = A ^ B;  // XOR_Gate xor_1, 32 bits wide
endmodule

module bloco_logico (
  input  [31:0] A,
  input  [31:0] B,
  input  [3:0] AluOp,
  output [31:0] S
);

  wire [31:0] and_32_bits_splitter_1_s, bit_extender_1_out, bit_extender_2_out, bit_extender_3_out,
       bit_extender_4_out, porta_nor_32_bits_splitter_1_s, porta_or_32_bits_splitter_1_s,
       porta_xor_32_bits_splitter_1_s;

  And_32_bits_splitter and_32_bits_splitter_1 (.A(A), .B(B), .S(and_32_bits_splitter_1_s));
  porta_or_32_bits_splitter porta_or_32_bits_splitter_1 (.A(A), .B(B), .S(porta_or_32_bits_splitter_1_s));
  porta_xor_32_bits_splitter porta_xor_32_bits_splitter_1 (.A(A), .B(B), .S(porta_xor_32_bits_splitter_1_s));
  porta_nor_32_bits_splitter porta_nor_32_bits_splitter_1 (.A(A), .B(B), .S(porta_nor_32_bits_splitter_1_s));
  assign bit_extender_1_out = {{31{AluOp[0]}}, AluOp[0]};  // Bit_Extender bit_extender_1
  assign bit_extender_2_out = {{31{AluOp[1]}}, AluOp[1]};  // Bit_Extender bit_extender_2
  assign bit_extender_3_out = {{31{AluOp[2]}}, AluOp[2]};  // Bit_Extender bit_extender_3
  assign bit_extender_4_out = {{31{AluOp[3]}}, AluOp[3]};  // Bit_Extender bit_extender_4
  assign S = and_32_bits_splitter_1_s & ~bit_extender_1_out & ~bit_extender_2_out & bit_extender_3_out & ~bit_extender_4_out;  // AND_Gate and_1, 32 bits wide
  assign S = porta_or_32_bits_splitter_1_s & ~bit_extender_1_out & bit_extender_2_out & ~bit_extender_3_out & bit_extender_4_out;  // AND_Gate and_2, 32 bits wide
  assign S = porta_xor_32_bits_splitter_1_s & bit_extender_1_out & ~bit_extender_2_out & ~bit_extender_3_out & bit_extender_4_out;  // AND_Gate and_3, 32 bits wide
  assign S = porta_nor_32_bits_splitter_1_s & bit_extender_1_out & bit_extender_2_out & bit_extender_3_out & ~bit_extender_4_out;  // AND_Gate and_4, 32 bits wide

  // Notes on the sheet:
  //   Entradas de A e B de 0 a 31
  //   <-Bit MSB à esquerda<-
  //   ->Bit LSB à direita->
  //   Bloco Lógico 
  //   operações lógicas
  //   seletor de entradas
  //   S3 S2 S1 S
  //   Saída do bitwise
endmodule
